// Logisim project RISC_V_CPU.circ as structural Verilog: 3 circuits, main circuit CPU
module CPU (
);

  wire [9:0] program_counter_1_out_5;

  Program_Counter program_counter_1 (.out_5(program_counter_1_out_5));  // open: in_2, in_3, in_4, in_1
  Instruction_Memory instruction_memory_1 (.in_1(program_counter_1_out_5));  // open: out_2
endmodule

module Program_Counter (
  input  [9:0] in_1,
  input  in_2,
  input  in_3,
  input  in_4,
  output [9:0] out_5
);

  Counter #(.max('h3ff), .width(10)) counter_1 (
    .clr(in_2), .load(in_3), .clk(in_4), .D(in_1), .Q(out_5));  // open: up, count, carry

  // Other names for the same wires on the sheet: ADDR_IN[9:0] = in_1; ADDR_OUT[9:0] = out_5
endmodule

module Instruction_Memory (
  input  [9:0] in_1,
  output [31:0] out_2
);

  ROM #(.addrWidth(10), .dataWidth(32)) rom_1 (.addr(in_1), .data(out_2));

  // Other names for the same wires on the sheet: ADDR_IN[9:0] = in_1; ADDR_OUT[31:0] = out_2
endmodule
